// Logisim project Thavy_Thach_xMM_FINAL_Project.circ as structural Verilog: 7 circuits, main circuit main
module main (
  input  [15:0] Carry_In,
  input  [15:0] X,
  input  [15:0] Y,
  output [15:0] Z,
  output [15:0] Carry_Out
);

  wire clock_1_out;

  Clock clock_1 (.out(clock_1_out));
  DotMatrix #(.matrixcols(1), .matrixrows(1)) dotmatrix_1 (.col0(clock_1_out));
  DotMatrix #(.matrixcols(1), .matrixrows(1)) dotmatrix_2 (.col0(clock_1_out));
  DotMatrix #(.matrixcols(1), .matrixrows(1)) dotmatrix_3 (.col0(clock_1_out));
  DotMatrix #(.matrixcols(1), .matrixrows(1)) dotmatrix_4 (.col0(clock_1_out));
  DotMatrix #(.matrixcols(1), .matrixrows(1)) dotmatrix_5 (.col0(clock_1_out));
  DotMatrix #(.matrixcols(1), .matrixrows(1)) dotmatrix_6 (.col0(clock_1_out));
  DotMatrix #(.matrixcols(1), .matrixrows(1)) dotmatrix_7 (.col0(clock_1_out));
  DotMatrix #(.matrixcols(1), .matrixrows(1)) dotmatrix_8 (.col0(clock_1_out));
  DotMatrix #(.matrixcols(1), .matrixrows(1)) dotmatrix_9 (.col0(clock_1_out));
  DotMatrix #(.matrixcols(1), .matrixrows(1)) dotmatrix_10 (.col0(clock_1_out));
  DotMatrix #(.matrixcols(1), .matrixrows(1)) dotmatrix_11 (.col0(clock_1_out));
  DotMatrix #(.matrixcols(1), .matrixrows(1)) dotmatrix_12 (.col0(clock_1_out));
  DotMatrix #(.matrixcols(1), .matrixrows(1)) dotmatrix_13 (.col0(clock_1_out));
  DotMatrix #(.matrixcols(1), .matrixrows(1)) dotmatrix_14 (.col0(clock_1_out));
  DotMatrix #(.matrixcols(1), .matrixrows(1)) dotmatrix_15 (.col0(clock_1_out));
  DotMatrix #(.matrixcols(1), .matrixrows(1)) dotmatrix_16 (.col0(clock_1_out));
  DotMatrix #(.matrixcols(1), .matrixrows(1)) dotmatrix_17 (.col0(clock_1_out));
  DotMatrix #(.matrixcols(1), .matrixrows(1)) dotmatrix_18 (.col0(clock_1_out));
  DotMatrix #(.matrixcols(1), .matrixrows(1)) dotmatrix_19 (.col0(clock_1_out));
  DotMatrix #(.matrixcols(1), .matrixrows(1)) dotmatrix_20 (.col0(clock_1_out));
  DotMatrix #(.matrixcols(1), .matrixrows(1)) dotmatrix_21 (.col0(clock_1_out));
  DotMatrix #(.matrixcols(1), .matrixrows(1)) dotmatrix_22 (.col0(clock_1_out));
  DotMatrix #(.matrixcols(1), .matrixrows(1)) dotmatrix_23 (.col0(clock_1_out));
  DotMatrix #(.matrixcols(1), .matrixrows(1)) dotmatrix_24 (.col0(clock_1_out));
  DotMatrix #(.matrixcols(1), .matrixrows(1)) dotmatrix_25 (.col0(clock_1_out));
  DotMatrix #(.matrixcols(1), .matrixrows(1)) dotmatrix_26 (.col0(clock_1_out));
  DotMatrix #(.matrixcols(1), .matrixrows(1)) dotmatrix_27 (.col0(clock_1_out));
  DotMatrix #(.matrixcols(1), .matrixrows(1)) dotmatrix_28 (.col0(clock_1_out));
  Clock #(.highDuration(2)) clock_2 (.out(clock_1_out));
  Hex_Digit_Display hex_digit_display_1 (.value(X[15:12]));  // open: dp
  Hex_Digit_Display hex_digit_display_2 (.value(Y[15:12]));  // open: dp
  Hex_Digit_Display hex_digit_display_3 (.value(X[11:8]));  // open: dp
  Hex_Digit_Display hex_digit_display_4 (.value(X[7:4]));  // open: dp
  Hex_Digit_Display hex_digit_display_5 (.value(Y[7:4]));  // open: dp
  Hex_Digit_Display hex_digit_display_6 (.value(Y[11:8]));  // open: dp
  Hex_Digit_Display hex_digit_display_7 (.value(X[3:0]));  // open: dp
  Hex_Digit_Display hex_digit_display_8 (.value(Y[3:0]));  // open: dp
  Hex_Digit_Display hex_digit_display_9 (.value(Carry_Out[15:12]));  // open: dp
  Hex_Digit_Display hex_digit_display_10 (.value(Carry_Out[11:8]));  // open: dp
  Hex_Digit_Display hex_digit_display_11 (.value(Carry_Out[7:4]));  // open: dp
  Hex_Digit_Display hex_digit_display_12 (.value(Carry_In[15:12]));  // open: dp
  Hex_Digit_Display hex_digit_display_13 (.value(Carry_In[11:8]));  // open: dp
  _16_bit__Bit_By_Bot u_16_bit_bit_by_bot_1 (
    .begin_multiplier(X), .begin_multiplicand(Y), .Carry_In(Carry_In), .Answer(Z), .Carry_Out(Carry_Out));
  Hex_Digit_Display hex_digit_display_14 (.value(Carry_Out[3:0]));  // open: dp
  Hex_Digit_Display hex_digit_display_15 (.value(Carry_In[7:4]));  // open: dp
  Hex_Digit_Display hex_digit_display_16 (.value(Carry_In[3:0]));  // open: dp
  Hex_Digit_Display hex_digit_display_17 (.value(Z[15:12]));  // open: dp
  Hex_Digit_Display hex_digit_display_18 (.value(Z[11:8]));  // open: dp
  Hex_Digit_Display hex_digit_display_19 (.value(Z[7:4]));  // open: dp
  Hex_Digit_Display hex_digit_display_20 (.value(Z[3:0]));  // open: dp
  Clock clock_3 (.out(clock_1_out));
  DotMatrix #(.matrixcols(1), .matrixrows(1)) dotmatrix_29 (.col0(clock_1_out));
  DotMatrix #(.matrixcols(1), .matrixrows(1)) dotmatrix_30 (.col0(clock_1_out));
  DotMatrix #(.matrixcols(1), .matrixrows(1)) dotmatrix_31 (.col0(clock_1_out));
  DotMatrix #(.matrixcols(1), .matrixrows(1)) dotmatrix_32 (.col0(clock_1_out));
  DotMatrix #(.matrixcols(1), .matrixrows(1)) dotmatrix_33 (.col0(clock_1_out));
  DotMatrix #(.matrixcols(1), .matrixrows(1)) dotmatrix_34 (.col0(clock_1_out));
  DotMatrix #(.matrixcols(1), .matrixrows(1)) dotmatrix_35 (.col0(clock_1_out));
  DotMatrix #(.matrixcols(1), .matrixrows(1)) dotmatrix_36 (.col0(clock_1_out));
  DotMatrix #(.matrixcols(1), .matrixrows(1)) dotmatrix_37 (.col0(clock_1_out));
  DotMatrix #(.matrixcols(1), .matrixrows(1)) dotmatrix_38 (.col0(clock_1_out));
  DotMatrix #(.matrixcols(1), .matrixrows(1)) dotmatrix_39 (.col0(clock_1_out));
  DotMatrix #(.matrixcols(1), .matrixrows(1)) dotmatrix_40 (.col0(clock_1_out));
  DotMatrix #(.matrixcols(1), .matrixrows(1)) dotmatrix_41 (.col0(clock_1_out));
  DotMatrix #(.matrixcols(1), .matrixrows(1)) dotmatrix_42 (.col0(clock_1_out));
  DotMatrix #(.matrixcols(1), .matrixrows(1)) dotmatrix_43 (.col0(clock_1_out));
  DotMatrix #(.matrixcols(1), .matrixrows(1)) dotmatrix_44 (.col0(clock_1_out));
  DotMatrix #(.matrixcols(1), .matrixrows(1)) dotmatrix_45 (.col0(clock_1_out));
  DotMatrix #(.matrixcols(1), .matrixrows(1)) dotmatrix_46 (.col0(clock_1_out));
  DotMatrix #(.matrixcols(1), .matrixrows(1)) dotmatrix_47 (.col0(clock_1_out));
  DotMatrix #(.matrixcols(1), .matrixrows(1)) dotmatrix_48 (.col0(clock_1_out));
  DotMatrix #(.matrixcols(1), .matrixrows(1)) dotmatrix_49 (.col0(clock_1_out));
  DotMatrix #(.matrixcols(1), .matrixrows(1)) dotmatrix_50 (.col0(clock_1_out));
  DotMatrix #(.matrixcols(1), .matrixrows(1)) dotmatrix_51 (.col0(clock_1_out));
  DotMatrix #(.matrixcols(1), .matrixrows(1)) dotmatrix_52 (.col0(clock_1_out));
  DotMatrix #(.matrixcols(1), .matrixrows(1)) dotmatrix_53 (.col0(clock_1_out));
  DotMatrix #(.matrixcols(1), .matrixrows(1)) dotmatrix_54 (.col0(clock_1_out));
  DotMatrix #(.matrixcols(1), .matrixrows(1)) dotmatrix_55 (.col0(clock_1_out));
  DotMatrix #(.matrixcols(1), .matrixrows(1)) dotmatrix_56 (.col0(clock_1_out));
  Clock clock_4 (.out(clock_1_out));

  // Notes on the sheet:
  //   Assembly Language And Architecture Final Project:
  //   HEX
  //   HEX
  //   CTRL + K
  //   MULTIPLIER
  //   HEX
  //   HEX
  //   Thavy Thach
endmodule

module _16_bit__Bit_By_Bot (
  input  [15:0] begin_multiplier,
  input  [15:0] begin_multiplicand,
  input  [15:0] Carry_In,
  output [15:0] Answer,
  output [15:0] Carry_Out
);

  wire adder_1_cout;
  wire [15:0] n32_bit_shift_prod_sll_1_multiplicand_2, n32_bit_shift_prod_sll_2_multiplicand_2,
       n32_bit_shift_prod_sll_3_multiplicand_2, n32_bit_shift_prod_sll_4_multiplicand_2,
       n32_bit_shift_prod_sll_5_multiplicand_2, n32_bit_shift_prod_sll_6_multiplicand_2,
       n32_bit_shift_prod_sll_7_multiplicand_2, n32_bit_shift_prod_sll_8_multiplicand_2,
       n32_bit_shift_prod_sll_9_multiplicand_2, n32_bit_shift_prod_sll_10_multiplicand_2,
       n32_bit_shift_prod_sll_11_multiplicand_2, n32_bit_shift_prod_sll_12_multiplicand_2,
       n32_bit_shift_prod_sll_13_multiplicand_2, n32_bit_shift_prod_sll_14_multiplicand_2,
       n32_bit_shift_prod_sll_15_multiplicand_2, n32_bit_shift_prod_sll_16_multiplicand_2;
  wire [31:0] n16_to_32_init_1_out_2, n32_bit_shift_prod_sll_1_shifted_product,
       n32_bit_shift_prod_sll_2_shifted_product, n32_bit_shift_prod_sll_3_shifted_product,
       n32_bit_shift_prod_sll_4_shifted_product, n32_bit_shift_prod_sll_5_shifted_product,
       n32_bit_shift_prod_sll_6_shifted_product, n32_bit_shift_prod_sll_7_shifted_product,
       n32_bit_shift_prod_sll_8_shifted_product, n32_bit_shift_prod_sll_9_shifted_product,
       n32_bit_shift_prod_sll_10_shifted_product, n32_bit_shift_prod_sll_11_shifted_product,
       n32_bit_shift_prod_sll_12_shifted_product, n32_bit_shift_prod_sll_13_shifted_product,
       n32_bit_shift_prod_sll_14_shifted_product, n32_bit_shift_prod_sll_15_shifted_product,
       n32_bit_shift_prod_sll_16_shifted_product;

  _16_to_32__Init u_16_to_32_init_1 (.begin_multiplier(begin_multiplier), .out_2(n16_to_32_init_1_out_2));
  _32_Bit__Shift_Prod___SLL u_32_bit_shift_prod_sll_1 (
    .Shifted_Product(n32_bit_shift_prod_sll_1_shifted_product), .Multiplicand(begin_multiplicand),
    .Multiplier(n16_to_32_init_1_out_2), .Multiplicand_2(n32_bit_shift_prod_sll_1_multiplicand_2));
  _32_Bit__Shift_Prod___SLL u_32_bit_shift_prod_sll_2 (
    .Shifted_Product(n32_bit_shift_prod_sll_2_shifted_product),
    .Multiplicand(n32_bit_shift_prod_sll_13_multiplicand_2),
    .Multiplier(n32_bit_shift_prod_sll_13_shifted_product),
    .Multiplicand_2(n32_bit_shift_prod_sll_2_multiplicand_2));
  _32_Bit__Shift_Prod___SLL u_32_bit_shift_prod_sll_3 (
    .Shifted_Product(n32_bit_shift_prod_sll_3_shifted_product),
    .Multiplicand(n32_bit_shift_prod_sll_14_multiplicand_2),
    .Multiplier(n32_bit_shift_prod_sll_14_shifted_product),
    .Multiplicand_2(n32_bit_shift_prod_sll_3_multiplicand_2));
  _32_Bit__Shift_Prod___SLL u_32_bit_shift_prod_sll_4 (
    .Shifted_Product(n32_bit_shift_prod_sll_4_shifted_product),
    .Multiplicand(n32_bit_shift_prod_sll_15_multiplicand_2),
    .Multiplier(n32_bit_shift_prod_sll_15_shifted_product),
    .Multiplicand_2(n32_bit_shift_prod_sll_4_multiplicand_2));
  _32_Bit__Shift_Prod___SLL u_32_bit_shift_prod_sll_5 (
    .Shifted_Product(n32_bit_shift_prod_sll_5_shifted_product),
    .Multiplicand(n32_bit_shift_prod_sll_1_multiplicand_2),
    .Multiplier(n32_bit_shift_prod_sll_1_shifted_product),
    .Multiplicand_2(n32_bit_shift_prod_sll_5_multiplicand_2));
  _32_Bit__Shift_Prod___SLL u_32_bit_shift_prod_sll_6 (
    .Shifted_Product(n32_bit_shift_prod_sll_6_shifted_product),
    .Multiplicand(n32_bit_shift_prod_sll_2_multiplicand_2),
    .Multiplier(n32_bit_shift_prod_sll_2_shifted_product),
    .Multiplicand_2(n32_bit_shift_prod_sll_6_multiplicand_2));
  _32_Bit__Shift_Prod___SLL u_32_bit_shift_prod_sll_7 (
    .Shifted_Product(n32_bit_shift_prod_sll_7_shifted_product),
    .Multiplicand(n32_bit_shift_prod_sll_3_multiplicand_2),
    .Multiplier(n32_bit_shift_prod_sll_3_shifted_product),
    .Multiplicand_2(n32_bit_shift_prod_sll_7_multiplicand_2));
  _32_Bit__Shift_Prod___SLL u_32_bit_shift_prod_sll_8 (
    .Shifted_Product(n32_bit_shift_prod_sll_8_shifted_product),
    .Multiplicand(n32_bit_shift_prod_sll_4_multiplicand_2),
    .Multiplier(n32_bit_shift_prod_sll_4_shifted_product),
    .Multiplicand_2(n32_bit_shift_prod_sll_8_multiplicand_2));
  _32_Bit__Shift_Prod___SLL u_32_bit_shift_prod_sll_9 (
    .Shifted_Product(n32_bit_shift_prod_sll_9_shifted_product),
    .Multiplicand(n32_bit_shift_prod_sll_5_multiplicand_2),
    .Multiplier(n32_bit_shift_prod_sll_5_shifted_product),
    .Multiplicand_2(n32_bit_shift_prod_sll_9_multiplicand_2));
  _32_Bit__Shift_Prod___SLL u_32_bit_shift_prod_sll_10 (
    .Shifted_Product(n32_bit_shift_prod_sll_10_shifted_product),
    .Multiplicand(n32_bit_shift_prod_sll_6_multiplicand_2),
    .Multiplier(n32_bit_shift_prod_sll_6_shifted_product),
    .Multiplicand_2(n32_bit_shift_prod_sll_10_multiplicand_2));
  _32_Bit__Shift_Prod___SLL u_32_bit_shift_prod_sll_11 (
    .Shifted_Product(n32_bit_shift_prod_sll_11_shifted_product),
    .Multiplicand(n32_bit_shift_prod_sll_7_multiplicand_2),
    .Multiplier(n32_bit_shift_prod_sll_7_shifted_product),
    .Multiplicand_2(n32_bit_shift_prod_sll_11_multiplicand_2));
  _32_Bit__Shift_Prod___SLL u_32_bit_shift_prod_sll_12 (
    .Shifted_Product(n32_bit_shift_prod_sll_12_shifted_product),
    .Multiplicand(n32_bit_shift_prod_sll_8_multiplicand_2),
    .Multiplier(n32_bit_shift_prod_sll_8_shifted_product),
    .Multiplicand_2(n32_bit_shift_prod_sll_12_multiplicand_2));
  _32_Bit__Shift_Prod___SLL u_32_bit_shift_prod_sll_13 (
    .Shifted_Product(n32_bit_shift_prod_sll_13_shifted_product),
    .Multiplicand(n32_bit_shift_prod_sll_9_multiplicand_2),
    .Multiplier(n32_bit_shift_prod_sll_9_shifted_product),
    .Multiplicand_2(n32_bit_shift_prod_sll_13_multiplicand_2));
  _32_Bit__Shift_Prod___SLL u_32_bit_shift_prod_sll_14 (
    .Shifted_Product(n32_bit_shift_prod_sll_14_shifted_product),
    .Multiplicand(n32_bit_shift_prod_sll_10_multiplicand_2),
    .Multiplier(n32_bit_shift_prod_sll_10_shifted_product),
    .Multiplicand_2(n32_bit_shift_prod_sll_14_multiplicand_2));
  _32_Bit__Shift_Prod___SLL u_32_bit_shift_prod_sll_15 (
    .Shifted_Product(n32_bit_shift_prod_sll_15_shifted_product),
    .Multiplicand(n32_bit_shift_prod_sll_11_multiplicand_2),
    .Multiplier(n32_bit_shift_prod_sll_11_shifted_product),
    .Multiplicand_2(n32_bit_shift_prod_sll_15_multiplicand_2));
  _32_Bit__Shift_Prod___SLL u_32_bit_shift_prod_sll_16 (
    .Shifted_Product(n32_bit_shift_prod_sll_16_shifted_product),
    .Multiplicand(n32_bit_shift_prod_sll_12_multiplicand_2),
    .Multiplier(n32_bit_shift_prod_sll_12_shifted_product),
    .Multiplicand_2(n32_bit_shift_prod_sll_16_multiplicand_2));
  Adder #(.width(16)) adder_1 (
    .a(Carry_In), .b(n32_bit_shift_prod_sll_16_shifted_product[15:0]), .out(Answer), .cout(adder_1_cout));  // open: cin
  Adder #(.width(16)) adder_2 (
    .a(n32_bit_shift_prod_sll_16_shifted_product[31:16]), .b({16{1'b0}}), .out(Carry_Out), .cin(adder_1_cout));  // open: cout

  // Notes on the sheet:
  //   Unused
endmodule

module _16_to_32__Init (
  input  [15:0] begin_multiplier,
  output [31:0] out_2
);

  wire [31:0] bit_extender_1_out;

  assign bit_extender_1_out = {{16{1'b0}}, begin_multiplier};  // Bit_Extender bit_extender_1
  Adder #(.width(32)) adder_1 (.a({32{1'b0}}), .b(bit_extender_1_out), .out(out_2));  // open: cin, cout
endmodule

module _16_to_32__SLL_4_MULTIPLICAND (
  input  [15:0] multiplicand,
  output [31:0] SLL_4
);

  wire [31:0] bit_extender_1_out;

  assign bit_extender_1_out = {{16{1'b0}}, multiplicand};  // Bit_Extender bit_extender_1
  Shifter #(.width(32)) shifter_1 (.in(bit_extender_1_out), .\dist (5'b10000), .out(SLL_4));
endmodule

module _32_bit__NO_OP_ADD_TO_PROD (
  input  [31:0] Multiplicand,
  input  [31:0] Product,
  output [15:0] Multiplicand_2,
  output [31:0] Product_2,
  output out_5
);

  wire [31:0] and_1_out;

  assign and_1_out = {32{Product[0]}} & Multiplicand;  // AND_Gate and_1, 32 bits wide
  Adder #(.width(32)) adder_1 (.a(and_1_out), .b(Product), .out(Product_2), .cout(out_5));  // open: cin

  assign Multiplicand_2 = Multiplicand[31:16];
endmodule

module _32_bit__SRL_1 (
  input  [31:0] Product,
  output [31:0] Shifted_Product
);

  Shifter #(.width(32), .shift("lr")) shifter_1 (.in(Product), .\dist (5'b00001), .out(Shifted_Product));
endmodule

module _32_Bit__Shift_Prod___SLL (
  input  [15:0] Multiplicand,
  input  [31:0] Multiplier,
  output [31:0] Shifted_Product,
  output [15:0] Multiplicand_2
);

  wire [31:0] n16_to_32_sll_4_multiplicand_1_sll_4, n32_bit_no_op_add_to_prod_1_product_2;

  _16_to_32__SLL_4_MULTIPLICAND u_16_to_32_sll_4_multiplicand_1 (
    .multiplicand(Multiplicand), .SLL_4(n16_to_32_sll_4_multiplicand_1_sll_4));
  _32_bit__NO_OP_ADD_TO_PROD u_32_bit_no_op_add_to_prod_1 (
    .Multiplicand(n16_to_32_sll_4_multiplicand_1_sll_4), .Product(Multiplier),
    .Product_2(n32_bit_no_op_add_to_prod_1_product_2), .Multiplicand_2(Multiplicand_2));  // open: out_5
  _32_bit__SRL_1 u_32_bit_srl_1_1 (.Product(n32_bit_no_op_add_to_prod_1_product_2), .Shifted_Product(Shifted_Product));
endmodule
